# Fritzing sketch diagramacao-horta (saved by Fritzing 1.0.4)

parts:
  esp1 = ESP32 DevKitc V4
  Componente1 = Soil Moisture Sensor
  Componente2 = Soil Moisture Sensor
  M2 = 1 chan 5v relay module
  WATER_PUMP1 = water pump/motor  # not connected
  VCC2 = 4 x AAA Battery Mount [internal_resistance=0.1Ω]  # not connected
  M1 = keystudio esp32 i/o shield
  M3 = CK-07 [package=THT]
  M4 = CK-07 [package=THT]
  VCC1 = 4 x AAA Battery Mount [internal_resistance=0.1Ω]
  Componente3 = LCD1602-I2C

nets:
  5V: esp1.5V, M1.3V3, M1.3.3V, M3.pin_4, M4.pin_4, Componente3.VCC
  N1: Componente1.GND, M4.pin_5
  N2: Componente1.VCC, M4.pin_6
  N3: Componente2.GND, M3.pin_5
  N4: Componente2.VCC, M3.pin_6
  N5: M2.pin_1, M1.5V
  GND: M2.pin_2, M1.GND, M3.pin_3, M4.pin_3, Componente3.GND
  N6: M2.pin_3, M1.IO25
  N7: M2.pin_5, VCC1.+
  N8: M2.pin_6, VCC1.-
  N9: M1.IO32, M4.pin_1
  N10: M1.IO33, M3.pin_1
  N11: M1.IO21, Componente3.SDA
  N12: M1.IO22, Componente3.SCL

custom parts:
  ESP32 DevKitc V4: ESP32-DevKitC board with ESP32-WROOM-32 module. ESP32-DevKitC V4 is a small-sized ESP32-based development board produced by Espressif. Most of the pins on the ESP module are broken out to the pin headers on the board. The pins D0, D1, D2, D3, CMD and CLK are used internally for communication between ESP32 and SPI flash memory. They are grouped on both sides near the USB connector. Avoid using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
  1 chan 5v relay module: 1 Channel 5V Relay Module Board Shield with Optocoupler Support High and Low Level Trigger for Arduino.
  water pump/motor: WATER PUMP BY ARDUBLOCKTR
  keystudio esp32 i/o shield: The ESP32-IO shield has brought out all the pins of keyestudio ESP32 Core board in the form of 2.54mm pin header. In order to connect other sensors easily, the ESP32-IO shield also has 2 rows of 2.54mm pin headers, powering external sensors/modules with DC 3.3V voltage.
  CK-07: Fc-51 Infrared Obstacle Avoidance Proximity Sensor module. IR transmitter led, receiver LED, lm393 compaitor and a pot. 3.3 V to 5V power.
  LCD1602-I2C: A standard character display, usually with 2x16 characters. Comes in many colors with LCM1602 IIC attached.

// code stored in the sketch: diagramacao-horta.ino
#include <Wire.h>
#include <LiquidCrystal_I2C.h>


#define col 16
#define lin  2
#define ende 0x27


#define s1 32         
#define s2 33         
#define rele 25       


LiquidCrystal_I2C lcd(ende, col, lin);


void setup() {
  pinMode(s1, INPUT);
  pinMode(s2, INPUT);
  pinMode(rele, OUTPUT);
  
  lcd.init();
  lcd.backlight();
  lcd.clear();


  Serial.begin(9600);


  lcd.setCursor(1, 1);
  lcd.print("Iniciando...");
  delay(1000);
  lcd.clear();
}


void loop() {
  int s_direito = analogRead(s2);
  int s_esquerdo = analogRead(s1);


  lcd.setCursor(0,0);
  lcd.print("s_direito: ");
  lcd.setCursor(11,0);
  lcd.print(s_direito);
  Serial.println(s_direito);  
  
  lcd.setCursor(0,1);
  lcd.print("s_esquerdo: ");
  lcd.setCursor(12, 1);
  lcd.print(s_esquerdo);
  Serial.println(s_esquerdo);
  delay(2000);


  if ((s_direito > 2000) || (s_esquerdo > 2000)) { 
    lcd.clear();
    lcd.setCursor(0, 0);
    lcd.print("Solo seco!");
    lcd.setCursor(0, 1);
    Serial.println("Lig. a bomba");
    digitalWrite(rele, HIGH);
    delay(5000);
    
    lcd.clear();
    lcd.setCursor(0, 0);
    lcd.println("Desl. a bomba");
    digitalWrite(rele, LOW);
    delay(5000);
    lcd.clear();
  } else {
    lcd.clear();
    lcd.setCursor(0, 0);
    lcd.print("Solo umido :)");
    delay(1000);
    lcd.clear();
  }


  delay(5000);
}
